# Fritzing sketch board (saved by Fritzing 1.0.1rc)
circuit board: 6.34081cm x 5.14177cm
breadboards: 1

parts:
  IC1 = IC, DIP package, 6 pins [chip_label=IC]
  IC2 = IC, DIP package, 6 pins [chip_label=IC]
  IC3 = IC, DIP package, 6 pins [chip_label=IC]
  IC4 = IC, DIP package, 6 pins [chip_label=IC]
  IC5 = IC, DIP package, 6 pins [chip_label=IC]
  IC6 = IC, DIP package, 6 pins [chip_label=IC]
  IC7 = IC, DIP package, 6 pins [chip_label=IC]
  IC8 = IC, DIP package, 6 pins [chip_label=IC]
  J1 = screw terminal, 10 pins
  Mod1 = Raspberry Pi Pico W

nets:
  N1: IC1.pin1, IC2.pin1, IC3.pin1, IC4.pin1, IC5.pin1, IC6.pin1, IC7.pin1, IC8.pin1, J1.pin10
  N2: IC1.pin2, J1.pin9
  N3: IC1.pin4, Mod1.pin_12
  N4: IC1.pin5, IC2.pin5, IC3.pin5, IC4.pin5, IC5.pin5, IC6.pin5, IC7.pin5, IC8.pin5
  N5: IC1.pin6, IC2.pin6, IC3.pin6, IC4.pin6, IC5.pin6, IC6.pin6, IC7.pin6, IC8.pin6, Mod1.pin_36
  N6: IC2.pin2, J1.pin8
  N7: IC2.pin4, Mod1.pin_11
  N8: IC3.pin2, J1.pin7
  N9: IC3.pin4, Mod1.pin_10
  N10: IC4.pin2, J1.pin6
  N11: IC4.pin4, Mod1.pin_9
  N12: IC5.pin2, J1.pin5
  N13: IC5.pin4, Mod1.pin_7
  N14: IC6.pin2, J1.pin4
  N15: IC6.pin4, Mod1.pin_6
  N16: IC7.pin2, J1.pin3
  N17: IC7.pin4, Mod1.pin_5
  N18: IC8.pin2, J1.pin2
  N19: IC8.pin4, Mod1.pin_4
  N20: Mod1.pin_3, Mod1.pin_8, Mod1.pin_13, Mod1.pin_18, Mod1.pin_23, Mod1.pin_28, Mod1.pin_33, Mod1.pin_38

custom parts:
  Raspberry Pi Pico W: Raspberry Pi Pico W. Based around the RP2040 microcontroller the Pico W is a low cost microcontroller device bringing Raspberry Pi quality, cost, and easy of use to the microcontroller space. The areas marked KEEPOUT in pcb silkscreen should not have traces running through them to avoid shorts on a soldered in module!
